# Fritzing sketch GPIO_LED_Setup (saved by Fritzing 0.9.3b)
breadboards: 1

parts:
  Part1 = Adafruit T-Cobbler Plus [part_number="Adafruit #1989 and #2028"]
  Raspberry_Pi_1 = Raspberry Pi 3 [part_number=RPI-3-V1.2]
  LED1 = LED - 5mm [color="Red (633nm)" package="5 mm [THT]"]
  LED2 = LED - 5mm [color="Red (633nm)" package="5 mm [THT]"]
  R1 = Resistor [tolerance=±5% resistance=220 package=THT]
  R2 = Resistor [tolerance=±5% resistance=220 package=THT]

nets:
  3V3: Part1.+3.3V, Part1.+3.3V_2, Raspberry_Pi_1.3v3, Raspberry_Pi_1.3V3
  N1: Part1.GPIO5, Raspberry_Pi_1.GIPO5, LED2.anode
  N2: Part1.GPIO6, Raspberry_Pi_1.GIPO6, LED1.anode
  GND: Part1.GND, Raspberry_Pi_1.GND, R1.Pin_0, R2.Pin_0
  +5V: Part1.+5V, Raspberry_Pi_1.5V
  N3: Part1.SDA, Raspberry_Pi_1.GPIO2
  N4: Part1.SCL, Raspberry_Pi_1.GPIO3
  N5: Part1.GPIO4, Raspberry_Pi_1.GIPO4
  N6: Part1.TXD, Raspberry_Pi_1.GIPO14
  N7: Part1.RXD, Raspberry_Pi_1.GIPO15
  N8: Part1.GPIO17, Raspberry_Pi_1.GIPO17
  N9: Part1.GPIO18, Raspberry_Pi_1.GIPO18
  N10: Part1.GPIO27, Raspberry_Pi_1.GIPO27
  N11: Part1.GPIO22, Raspberry_Pi_1.GIPO22
  N12: Part1.GPIO23, Raspberry_Pi_1.GIPO23
  N13: Part1.GPIO24, Raspberry_Pi_1.GIPO24
  N14: Part1.MOSI, Raspberry_Pi_1.GIPO10
  N15: Part1.MISO, Raspberry_Pi_1.GIPO9
  N16: Part1.GPIO25, Raspberry_Pi_1.GIPO25
  N17: Part1.SCLK, Raspberry_Pi_1.GIPO11
  N18: Part1.CE0, Raspberry_Pi_1.GIPO8
  N19: Part1.CE1, Raspberry_Pi_1.GIPO7
  N20: Part1.EEDAT, Raspberry_Pi_1.ID_SD
  N21: Part1.EECLK, Raspberry_Pi_1.ID_SC
  N22: Part1.GPIO12, Raspberry_Pi_1.GIPO12
  N23: Part1.GPIO13, Raspberry_Pi_1.GIPO13
  N24: Part1.GPIO19, Raspberry_Pi_1.GIPO19
  N25: Part1.GPIO16, Raspberry_Pi_1.GIPO16
  N26: Part1.GPIO26, Raspberry_Pi_1.GIPO26
  N27: Part1.GPIO20, Raspberry_Pi_1.GIPO20
  N28: Part1.GPIO21, Raspberry_Pi_1.GIPO21
  N29: LED1.cathode, R2.Pin_1
  N30: LED2.cathode, R1.Pin_1

custom parts:
  Adafruit T-Cobbler Plus: The Raspberry Pi has landed on the Maker World like a 40-GPIO pinned, quad-USB ported, credit card sized bomb of DIY joy. And while you can use most of our great Model B accessories by hooking up our downgrade cable, its probably a good time to upgrade your set up and accessorize using all of the 40 pins. That's why we now carry the Assembled Adafruit Pi T-Cobbler Plus - Breakout + Cable for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
